// Logisim project Additionneur1bitCin.circ as structural Verilog
module Addictionneur2Variables (
  input  in_1,
  input  in_2,
  output Res,
  output Cout
);

  xor xor_1 (Res, in_1, in_2);
  and and_1 (Cout, in_1, in_2);
endmodule

module Addictionneur3Variables (
  input  A,
  input  B,
  input  Cin,
  output Res,
  output Cout
);

  wire and_1_out, Cin___A___B_out, Cin___A_out, Cin___B_out, or_1_out, or_2_out, xor_1_out;

  xor xor_1 (xor_1_out, A, B);
  and and_1 (and_1_out, A, B);
  and Cin___B (Cin___B_out, Cin, B);
  and Cin___A (Cin___A_out, Cin, A);
  and Cin___A___B (Cin___A___B_out, A, Cin, B);
  xor xor_2 (Res, xor_1_out, Cin);
  or or_1 (or_1_out, and_1_out, Cin___B_out);
  or or_2 (or_2_out, Cin___A_out, Cin___A___B_out);
  or or_3 (Cout, or_1_out, or_2_out);

  // Notes on the sheet:
  //   A
  //   B
  //   CIN
  //   A & B
endmodule

// ADDITIONNEUR
module Additionneur4bits (
  input  [3:0] in_1,
  input  [3:0] in_2,
  output [4:0] out_3
);

  wire addictionneur2variables_1_cout, addictionneur3variables_2_cout, addictionneur3variables_3_cout;

  Addictionneur3Variables addictionneur3variables_1 (
    .A(in_1[3]), .B(in_2[3]), .Cin(addictionneur3variables_2_cout), .Res(out_3[3]), .Cout(out_3[4]));
  Addictionneur3Variables addictionneur3variables_2 (
    .A(in_1[2]), .B(in_2[2]), .Cin(addictionneur3variables_3_cout), .Res(out_3[2]),
    .Cout(addictionneur3variables_2_cout));
  Addictionneur3Variables addictionneur3variables_3 (
    .A(in_1[1]), .B(in_2[1]), .Cin(addictionneur2variables_1_cout), .Res(out_3[1]),
    .Cout(addictionneur3variables_3_cout));
  Addictionneur2Variables addictionneur2variables_1 (
    .in_1(in_1[0]), .in_2(in_2[0]), .Res(out_3[0]), .Cout(addictionneur2variables_1_cout));
endmodule

module TestAddition (
  input  in_1,
  input  in_2,
  output out_3
);

  wire or_1_out;

  or or_1 (or_1_out, in_1, in_2);
  not not_1 (out_3, or_1_out);
endmodule

module TestXor (
  input  in_1,
  input  in_2,
  output out_3
);

  wire not_1_out;

  not not_1 (not_1_out, in_1);
  and and_1 (out_3, not_1_out, in_2);
endmodule

module TestAnd (
  input  in_1,
  input  in_2,
  output out_3
);

  wire not_1_out;

  not not_1 (not_1_out, in_2);
  and and_1 (out_3, in_1, not_1_out);
endmodule

module TestOr (
  input  in_1,
  input  in_2,
  output out_3
);

  and and_1 (out_3, in_1, in_2);
endmodule

// AND
module And4bits (
  input  [3:0] in_1,
  input  [3:0] in_2,
  output [4:0] out_3
);

  wire not_1_out;

  and and_1 (out_3[3], in_1[3], in_2[3]);
  and and_2 (out_3[2], in_1[2], in_2[2]);
  and and_3 (out_3[1], in_1[1], in_2[1]);
  and and_4 (out_3[0], in_1[0], in_2[0]);
  not not_1 (not_1_out, out_3[3]);
  and and_5 (out_3[4], out_3[3], not_1_out);

  // Notes on the sheet:
  //   A
  //   B
endmodule

module TestTotal (
  input  in_1,
  input  in_2,
  output out_3,
  output out_4,
  output out_5,
  output out_6
);

  TestAddition testaddition_1 (.in_1(in_1), .in_2(in_2), .out_3(out_3));
  TestXor testxor_1 (.in_1(in_1), .in_2(in_2), .out_3(out_4));
  TestAnd testand_1 (.in_1(in_1), .in_2(in_2), .out_3(out_5));
  TestOr testor_1 (.in_1(in_1), .in_2(in_2), .out_3(out_6));
endmodule

module Execution (
  input  a4,
  input  a3,
  input  a2,
  input  a1,
  input  b4,
  input  b3,
  input  b2,
  input  b1,
  input  var2,
  input  var1,
  output V__Overflow,
  output N,
  output C,
  output res4,
  output res3,
  output res2,
  output res1
);

  wire additionneur4bits_1_p2, additionneur4bits_1_p4, additionneur4bits_1_p6, additionneur4bits_1_p8,
       additionneur4bits_1_p10, moduletest_1_p1, moduletest_1_p2, moduletest_1_p3, moduletest_1_p4,
       moduletest_1_p5, moduletest_1_p6, moduletest_1_p7, moduletest_1_p8, moduletest_1_p9, moduletest_1_p10,
       or4bits_1_p2, or4bits_1_p4, or4bits_1_p6, or4bits_1_p8, or4bits_1_p10, testtotal_1_out_3,
       testtotal_1_out_4, testtotal_1_out_5, testtotal_1_out_6;

  TestTotal testtotal_1 (
    .in_1(var1), .in_2(var2), .out_3(testtotal_1_out_3), .out_4(testtotal_1_out_4),
    .out_5(testtotal_1_out_5), .out_6(testtotal_1_out_6));
  // Additionneur4bits additionneur4bits_1: pin names not known; wires that end beside it: b2, additionneur4bits_1_p2, b1, additionneur4bits_1_p4, a4, additionneur4bits_1_p6, a3, additionneur4bits_1_p8, a2, additionneur4bits_1_p10, a1
  // Or4bits or4bits_1: pin names not known; wires that end beside it: b2, or4bits_1_p2, b1, or4bits_1_p4, a4, or4bits_1_p6, a3, or4bits_1_p8, a2, or4bits_1_p10, a1
  // ModuleTest moduletest_1: pin names not known; wires that end beside it: moduletest_1_p1, moduletest_1_p2, moduletest_1_p3, moduletest_1_p4, moduletest_1_p5, moduletest_1_p6, moduletest_1_p7, moduletest_1_p8, moduletest_1_p9, moduletest_1_p10, or4bits_1_p2, V__Overflow, or4bits_1_p4, res4, or4bits_1_p6, res3, or4bits_1_p8, res2, or4bits_1_p10, res1, additionneur4bits_1_p10, additionneur4bits_1_p8, additionneur4bits_1_p6, additionneur4bits_1_p4, additionneur4bits_1_p2, testtotal_1_out_4, testtotal_1_out_5, testtotal_1_out_6, testtotal_1_out_3
  // And4bits and4bits_1: pin names not known; wires that end beside it: b2, moduletest_1_p6, b1, moduletest_1_p7, a4, moduletest_1_p8, a3, moduletest_1_p9, a2, moduletest_1_p10, a1
  // Xor4bits xor4bits_1: pin names not known; wires that end beside it: b2, moduletest_1_p1, b1, moduletest_1_p2, a4, moduletest_1_p3, a3, moduletest_1_p4, a2, moduletest_1_p5, a1

  // Notes on the sheet:
  //   A
  //   B
endmodule

// OR
module Or4bits (
  input  [3:0] in_1,
  input  [3:0] in_2,
  output [4:0] out_3
);

  wire not_1_out;

  or or_1 (out_3[3], in_1[3], in_2[3]);
  or or_2 (out_3[2], in_1[2], in_2[2]);
  or or_3 (out_3[1], in_1[1], in_2[1]);
  or or_4 (out_3[0], in_1[0], in_2[0]);
  not not_1 (not_1_out, out_3[3]);
  and and_1 (out_3[4], out_3[3], not_1_out);

  // Notes on the sheet:
  //   A
  //   B
endmodule

// XOR
module Xor4bits (
  input  [3:0] in_1,
  input  [3:0] in_2,
  output [4:0] out_3
);

  wire not_1_out;

  xor xor_1 (out_3[3], in_1[3], in_2[3]);
  xor xor_2 (out_3[2], in_1[2], in_2[2]);
  xor xor_3 (out_3[1], in_1[1], in_2[1]);
  xor xor_4 (out_3[0], in_1[0], in_2[0]);
  not not_1 (not_1_out, out_3[3]);
  and and_1 (out_3[4], out_3[3], not_1_out);

  // Notes on the sheet:
  //   A
  //   B
endmodule

module Test4variables (
  input  C,
  input  A,
  input  B,
  input  in_4,
  input  in_5,
  input  A_2,
  input  B_2,
  input  C_2,
  input  D,
  output Res,
  output Res_2
);

  wire and_1_out, and_2_out, and_3_out, and_4_out, and_5_out, and_6_out, and_7_out, and_8_out, and_9_out,
       and_10_out, and_11_out, and_12_out, not_1_out, testtotal_1_out_3, testtotal_1_out_4,
       testtotal_1_out_5, testtotal_1_out_6;

  TestTotal testtotal_1 (
    .in_1(in_5), .in_2(in_4), .out_3(testtotal_1_out_3), .out_4(testtotal_1_out_4),
    .out_5(testtotal_1_out_5), .out_6(testtotal_1_out_6));
  not not_1 (not_1_out, C);
  and and_1 (and_1_out, testtotal_1_out_3, A_2);
  and and_2 (and_2_out, testtotal_1_out_4, B_2);
  and and_3 (and_3_out, testtotal_1_out_5, C_2);
  and and_4 (and_4_out, testtotal_1_out_6, D);
  and and_5 (and_5_out, C, A);
  and and_6 (and_6_out, not_1_out, B);
  and and_7 (and_7_out, A_2, and_1_out);
  and and_8 (and_8_out, B_2, and_2_out);
  and and_9 (and_9_out, C_2, and_3_out);
  and and_10 (and_10_out, D, and_4_out);
  and and_11 (and_11_out, A, A, and_5_out);
  and and_12 (and_12_out, and_6_out, B);
  or or_1 (Res, and_11_out, and_12_out);
  or or_2 (Res_2, and_7_out, and_8_out, and_9_out, and_10_out);
endmodule

module ModuleTest (
  input  ADD,
  input  OR,
  input  AND,
  input  XOR,
  input  ADD1,
  input  ADD2,
  input  ADD3,
  input  ADD4,
  input  ADDV,
  input  OR1,
  input  OR2,
  input  OR3,
  input  OR4,
  input  ORV,
  input  AND1,
  input  AND2,
  input  AND3,
  input  AND4,
  input  ANDV,
  input  XOR1,
  input  XOR2,
  input  XOR3,
  input  XOR4,
  input  XORV,
  output res1,
  output res2,
  output res3,
  output res4,
  output resV
);

  wire and_1_out, and_2_out, and_3_out, and_4_out, and_5_out, and_6_out, and_7_out, and_8_out, and_9_out,
       and_10_out, and_11_out, and_12_out, and_13_out, and_14_out, and_15_out, and_16_out, and_17_out,
       and_18_out, and_19_out, and_20_out, and_21_out, and_22_out, and_23_out, and_24_out, and_25_out,
       and_26_out, and_27_out, and_28_out, and_29_out, and_30_out, and_31_out, and_32_out, and_33_out,
       and_34_out, and_35_out, and_36_out, and_37_out, and_38_out, and_39_out, and_40_out;

  and and_1 (and_1_out, ADD, ADD1);
  and and_2 (and_2_out, ADD, ADD2);
  and and_3 (and_3_out, ADD3, ADD);
  and and_4 (and_4_out, ADD4, ADD);
  and and_5 (and_5_out, ADD, ADDV);
  and and_6 (and_6_out, OR, OR1);
  and and_7 (and_7_out, OR, OR2);
  and and_8 (and_8_out, OR3, OR);
  and and_9 (and_9_out, OR4, OR);
  and and_10 (and_10_out, OR, ORV);
  and and_11 (and_11_out, AND, AND1);
  and and_12 (and_12_out, AND, AND2);
  and and_13 (and_13_out, AND3, AND);
  and and_14 (and_14_out, AND4, AND);
  and and_15 (and_15_out, AND, ANDV);
  and and_16 (and_16_out, XOR, XOR1);
  and and_17 (and_17_out, XOR, XOR2);
  and and_18 (and_18_out, XOR3, XOR);
  and and_19 (and_19_out, XOR4, XOR);
  and and_20 (and_20_out, XORV, XOR);
  and and_21 (and_21_out, ADD2, ADD2, and_2_out);
  and and_22 (and_22_out, ADD1, and_1_out);
  and and_23 (and_23_out, ADD3, ADD3, and_3_out);
  and and_24 (and_24_out, and_4_out, ADD4);
  and and_25 (and_25_out, ADDV, and_5_out);
  and and_26 (and_26_out, OR1, and_6_out);
  and and_27 (and_27_out, OR2, and_7_out);
  and and_28 (and_28_out, OR3, OR3, and_8_out);
  and and_29 (and_29_out, and_9_out, OR4);
  and and_30 (and_30_out, ORV, and_10_out);
  and and_31 (and_31_out, AND1, and_11_out);
  and and_32 (and_32_out, AND2, and_12_out);
  and and_33 (and_33_out, AND3, AND3, and_13_out);
  and and_34 (and_34_out, and_14_out, AND4);
  and and_35 (and_35_out, ANDV, and_15_out);
  and and_36 (and_36_out, XOR1, and_16_out);
  and and_37 (and_37_out, XOR2, and_17_out);
  and and_38 (and_38_out, XOR3, XOR3, and_18_out);
  and and_39 (and_39_out, and_19_out, XOR4);
  and and_40 (and_40_out, XORV, and_20_out);
  or or_1 (res1, and_22_out, and_31_out, and_26_out, and_36_out);
  or or_2 (res2, and_21_out, and_27_out, and_32_out, and_37_out);
  or or_3 (res3, and_23_out, and_33_out, and_28_out, and_38_out);
  or or_4 (res4, and_39_out, and_34_out, and_24_out, and_29_out);
  or or_5 (resV, and_25_out, and_35_out, and_30_out, and_40_out);
endmodule

module Registre4bits (
  input  [3:0] In,
  input  Clock,
  output [3:0] Out
);

  D_Flip_Flop d_ff_1 (.clk(Clock), .D(In[0]), .Q(Out[0]));  // open: Qn, preset, en, reset
  D_Flip_Flop d_ff_2 (.clk(Clock), .D(In[1]), .Q(Out[1]));  // open: Qn, preset, en, reset
  D_Flip_Flop d_ff_3 (.clk(Clock), .D(In[2]), .Q(Out[2]));  // open: Qn, preset, en, reset
  D_Flip_Flop d_ff_4 (.clk(Clock), .D(In[3]), .Q(Out[3]));  // open: Qn, preset, en, reset
endmodule

module MultiplexerEntrer (
  input  [3:0] A,
  input  [3:0] B,
  input  [3:0] Signal,
  output [3:0] Out,
  output Overflow,
  output ZF,
  output SF,
  output [3:0] out_8
);

  wire and_1_out, not_1_out, not_2_out, not_3_out, not_4_out, or_1_out,
       \soustraction_1_sf__signed_flag_1____négatif ;
  wire [3:0] demultiplexer_1_out0, demultiplexer_1_out4, demultiplexer_1_out5, demultiplexer_1_out6,
       demultiplexer_1_out7, demultiplexer_1_out8, demultiplexer_1_out9, demultiplexer_1_out10,
       demultiplexer_1_out11, demultiplexer_2_out0, demultiplexer_2_out4, demultiplexer_2_out5,
       demultiplexer_2_out6, demultiplexer_2_out7, demultiplexer_2_out8, demultiplexer_2_out9,
       demultiplexer_2_out10, testmultiplicateur_1_out_3;
  wire [4:0] additionneur4bits_1_out_3, and4bits_1_out_3, or4bits_1_out_3, retournevariable_1_out,
       soustraction_1_res, \testegalité_1_out_3 , xor4bits_1_out_3;

  Demultiplexer #(.select(4), .width(4), .enable("false")) demultiplexer_1 (
    .out0(demultiplexer_1_out0), .out4(demultiplexer_1_out4), .out5(demultiplexer_1_out5),
    .out6(demultiplexer_1_out6), .out7(demultiplexer_1_out7), .out8(demultiplexer_1_out8),
    .out9(demultiplexer_1_out9), .out10(demultiplexer_1_out10), .out11(demultiplexer_1_out11), .in(A),
    .sel(Signal));  // open: out1, out2, out3, out12, out13, out14, out15
  Demultiplexer #(.select(4), .width(4), .enable("false")) demultiplexer_2 (
    .out0(demultiplexer_2_out0), .out4(demultiplexer_2_out4), .out5(demultiplexer_2_out5),
    .out6(demultiplexer_2_out6), .out7(demultiplexer_2_out7), .out8(demultiplexer_2_out8),
    .out9(demultiplexer_2_out9), .out10(demultiplexer_2_out10), .out11(out_8), .in(B), .sel(Signal));  // open: out1, out2, out3, out12, out13, out14, out15
  TestMultiplicateur testmultiplicateur_1 (
    .A(demultiplexer_1_out0), .B(demultiplexer_2_out0), .out_3(testmultiplicateur_1_out_3));
  Soustraction soustraction_1 (
    .A(demultiplexer_2_out4), .B(demultiplexer_1_out4), .Res(soustraction_1_res),
    .\SF__Signed_Flag_1____Négatif (\soustraction_1_sf__signed_flag_1____négatif ));
  RetourneVariable retournevariable_1 (.In(demultiplexer_1_out5), .Out(retournevariable_1_out));
  Additionneur4bits additionneur4bits_1 (
    .in_1(demultiplexer_1_out6), .in_2(demultiplexer_2_out6), .out_3(additionneur4bits_1_out_3));
  And4bits and4bits_1 (.in_1(demultiplexer_1_out7), .in_2(demultiplexer_2_out7), .out_3(and4bits_1_out_3));
  Or4bits or4bits_1 (.in_1(demultiplexer_1_out8), .in_2(demultiplexer_2_out8), .out_3(or4bits_1_out_3));
  Xor4bits xor4bits_1 (.in_1(demultiplexer_1_out9), .in_2(demultiplexer_2_out9), .out_3(xor4bits_1_out_3));
  \TestEgalité  \testegalité_1  (.A(demultiplexer_1_out11), .B(out_8), .out_3(\testegalité_1_out_3 ));
  Multiplexer #(.select(4), .width(5), .enable("false")) multiplexer_1 (
    .in0({1'b0, testmultiplicateur_1_out_3}), .in4(soustraction_1_res), .in5(retournevariable_1_out),
    .in6(additionneur4bits_1_out_3), .in7(and4bits_1_out_3), .in8(or4bits_1_out_3), .in9(xor4bits_1_out_3),
    .in10(5'b00001), .in11(\testegalité_1_out_3 ), .out({Overflow, Out}), .sel(Signal));  // open: in1, in2, in3, in12, in13, in14, in15
  not not_1 (not_1_out, Signal[0]);
  not not_2 (not_2_out, Signal[1]);
  not not_3 (not_3_out, Signal[3]);
  Multiplexer #(.enable("false")) multiplexer_2 (
    .in0(\soustraction_1_sf__signed_flag_1____négatif ), .in1(1'b0), .out(SF), .sel(not_4_out));
  and and_1 (and_1_out, not_1_out, not_2_out, Signal[2], not_3_out);
  not not_4 (not_4_out, and_1_out);
  not not_5 (ZF, or_1_out);
  or or_1 (or_1_out, Out[0], Overflow, Out[3], Out[2], Out[1]);

  // Notes on the sheet:
  //   0000 Multiplication
  //   0100 Soustraction
  //   0101 Retourne A
  //   1000  OR
  //   0110 ADD
  //   0111 AND
  //   1001 XOR
  //   1010 Init
  //   1011 Egalité = : Z -> 1
  //   ZF : Passe a 0 si A = B
  //   SF : Passe a 1 si le nombre est négatif
endmodule

module UAL (
  input  [3:0] A,
  input  [3:0] B,
  input  [3:0] OP,
  output Overflow,
  output [3:0] Out,
  output ZF,
  output SF
);

  MultiplexerEntrer multiplexerentrer_1 (
    .A(B), .B(A), .Signal(OP), .Out(Out), .Overflow(Overflow), .ZF(ZF), .SF(SF));  // open: out_8

  // Notes on the sheet:
  //   1000  OR
  //   0110 ADD
  //   0111 AND
  //   1001 XOR
  //   1010 Init
  //   0000 Multiplication
  //   0100 Soustraction
  //   0101 Retourne A
  //   1011 Egalité = : Z -> 1
endmodule

module Additionneur8Bits_1Bit (
  input  in_1,
  input  [7:0] in_2,
  output [7:0] out_3
);

  wire addictionneur2variables_1_cout, addictionneur3variables_2_cout, addictionneur3variables_3_cout,
       addictionneur3variables_4_cout, addictionneur3variables_5_cout, addictionneur3variables_6_cout,
       addictionneur3variables_7_cout;

  Addictionneur3Variables addictionneur3variables_1 (
    .A(1'b0), .B(in_2[7]), .Cin(addictionneur3variables_2_cout), .Res(out_3[7]));  // open: Cout
  Addictionneur3Variables addictionneur3variables_2 (
    .A(in_2[6]), .B(1'b0), .Cin(addictionneur3variables_3_cout), .Res(out_3[6]),
    .Cout(addictionneur3variables_2_cout));
  Addictionneur3Variables addictionneur3variables_3 (
    .A(1'b0), .B(in_2[5]), .Cin(addictionneur3variables_4_cout), .Res(out_3[5]),
    .Cout(addictionneur3variables_3_cout));
  Addictionneur3Variables addictionneur3variables_4 (
    .A(in_2[4]), .B(1'b0), .Cin(addictionneur3variables_5_cout), .Res(out_3[4]),
    .Cout(addictionneur3variables_4_cout));
  Addictionneur3Variables addictionneur3variables_5 (
    .A(in_2[3]), .B(1'b0), .Cin(addictionneur3variables_6_cout), .Res(out_3[3]),
    .Cout(addictionneur3variables_5_cout));
  Addictionneur3Variables addictionneur3variables_6 (
    .A(1'b0), .B(in_2[2]), .Cin(addictionneur3variables_7_cout), .Res(out_3[2]),
    .Cout(addictionneur3variables_6_cout));
  Addictionneur3Variables addictionneur3variables_7 (
    .A(1'b0), .B(in_2[1]), .Cin(addictionneur2variables_1_cout), .Res(out_3[1]),
    .Cout(addictionneur3variables_7_cout));
  Addictionneur2Variables addictionneur2variables_1 (
    .in_1(in_1), .in_2(in_2[0]), .Res(out_3[0]), .Cout(addictionneur2variables_1_cout));
endmodule

module Compteur8BitsSansJump (
  input  Clock,
  input  Start,
  output [7:0] Instructions
);

  wire and_2_out, and_3_out, multiplexer_2_out, not_1_out, or_1_out;
  wire [7:0] Additionneur_out_3, and_1_out, multiplexer_1_out;

  or or_1 (or_1_out, Clock, and_3_out);
  Additionneur8Bits_1Bit Additionneur (.in_1(Clock), .in_2(Instructions), .out_3(Additionneur_out_3));
  Multiplexer #(.width(8), .enable("false")) multiplexer_1 (
    .in0(Additionneur_out_3), .in1({8{1'b0}}), .out(multiplexer_1_out), .sel(Start));
  not not_1 (not_1_out, or_1_out);
  Multiplexer #(.enable("false")) multiplexer_2 (.in0(not_1_out), .in1(Clock), .out(multiplexer_2_out), .sel(Start));
  Registre8Bits registre8bits_1 (.In(multiplexer_1_out), .Clock(multiplexer_2_out), .Out(Instructions));
  assign and_1_out = {8{1'b1}} & Instructions;  // AND_Gate and_1, 8 bits wide
  and and_2 (and_2_out, and_1_out[7], and_1_out[6], and_1_out[5], and_1_out[4], and_1_out[3]);
  and and_3 (and_3_out, and_2_out, and_1_out[2], and_1_out[1], and_1_out[0]);
endmodule

module ProcesseurSansRAM (
  input  Start,
  output [7:0] out_2,
  output out_3,
  output out_4,
  output out_5
);

  wire clock_1_out;
  wire [1:0] decodeursansram_1_a, decodeursansram_1_b, decodeursansram_1_registre;
  wire [3:0] decodeursansram_1_op;
  wire [9:0] ram_1_data;

  Clock clock_1 (.out(clock_1_out));
  RAM #(.dataWidth(10)) ram_1 (.addr(out_2), .data(ram_1_data));  // open: sel, clk, ld, clr
  Traitement traitement_1 (.in_1(out_2), .Init(out_3), .\Terminé (out_5), .En_cours(out_4));
  Compteur8BitsSansJump Compteur (.Clock(clock_1_out), .Start(Start), .Instructions(out_2));
  DecodeurSansRam decodeursansram_1 (
    .in_1(ram_1_data), .OP(decodeursansram_1_op), .B(decodeursansram_1_b), .A(decodeursansram_1_a),
    .Registre(decodeursansram_1_registre));
  UniteCommandeSansRAM Unite_de_commande (
    .Clock(clock_1_out), .Registre(decodeursansram_1_registre), .A(decodeursansram_1_a),
    .B(decodeursansram_1_b), .OP(decodeursansram_1_op));

  // Other names for the same wires on the sheet: En_cours = out_4; Init = out_3; Terminé = out_5

  // Notes on the sheet:
  //   100 OR
  //   010 ADD
  //   011 AND
  //   101 XOR
  //   110 Init
  //   Jeux d'instructions
  //   2 b => Registre / 2 b => A / 2 b =>B / 3 b => OP 
endmodule

module Registre (
  input  [3:0] Value,
  input  Clock,
  input  [1:0] SignalRegistre,
  output [3:0] out_4,
  output [3:0] out_5,
  output [3:0] out_6,
  output [3:0] out_7
);

  wire demultiplexer_1_out0, demultiplexer_1_out1, demultiplexer_1_out2, demultiplexer_1_out3;
  wire [3:0] demultiplexer_2_out0, demultiplexer_2_out1, demultiplexer_2_out2, demultiplexer_2_out3;

  Demultiplexer #(.select(2), .enable("false")) demultiplexer_1 (
    .out0(demultiplexer_1_out0), .out1(demultiplexer_1_out1), .out2(demultiplexer_1_out2),
    .out3(demultiplexer_1_out3), .in(Clock), .sel(SignalRegistre));
  Demultiplexer #(.select(2), .width(4), .enable("false")) demultiplexer_2 (
    .out0(demultiplexer_2_out0), .out1(demultiplexer_2_out1), .out2(demultiplexer_2_out2),
    .out3(demultiplexer_2_out3), .in(Value), .sel(SignalRegistre));
  Registre4bits registre4bits_1 (.In(demultiplexer_2_out0), .Clock(demultiplexer_1_out0), .Out(out_4));
  Registre4bits registre4bits_2 (.In(demultiplexer_2_out1), .Clock(demultiplexer_1_out1), .Out(out_5));
  Registre4bits registre4bits_3 (.In(demultiplexer_2_out2), .Clock(demultiplexer_1_out2), .Out(out_6));
  Registre4bits registre4bits_4 (.In(demultiplexer_2_out3), .Clock(demultiplexer_1_out3), .Out(out_7));
endmodule

module Registre8Bits (
  input  [7:0] In,
  input  Clock,
  output [7:0] Out
);

  Registre4bits registre4bits_1 (.In(In[3:0]), .Clock(Clock), .Out(Out[3:0]));
  Registre4bits registre4bits_2 (.In(In[7:4]), .Clock(Clock), .Out(Out[7:4]));
endmodule

module UniteCommandeSansRAM (
  input  Clock,
  input  [1:0] Registre,
  input  [1:0] A,
  input  [1:0] B,
  input  [3:0] OP
);

  wire [3:0] AccesRegistre_2_out, AccesRegistre_out, Registre_out_4, Registre_out_5, Registre_out_6,
       Registre_out_7, UAL_out;

  Registre u_Registre (
    .Value(UAL_out), .Clock(Clock), .SignalRegistre(Registre), .out_4(Registre_out_4),
    .out_5(Registre_out_5), .out_6(Registre_out_6), .out_7(Registre_out_7));
  AccesRegistre AccesRegistre (
    ._11(Registre_out_7), ._00(Registre_out_4), ._01(Registre_out_5), ._10(Registre_out_6), .Signal(A),
    .Out(AccesRegistre_out));
  AccesRegistre AccesRegistre_2 (
    ._11(Registre_out_7), ._00(Registre_out_4), ._01(Registre_out_5), ._10(Registre_out_6), .Signal(B),
    .Out(AccesRegistre_2_out));
  UAL UAL (.OP(OP), .A(AccesRegistre_out), .B(AccesRegistre_2_out), .Out(UAL_out));  // open: Overflow, ZF, SF

  // Notes on the sheet:
  //   100 OR
  //   010 ADD
  //   011 AND
  //   101 XOR
  //   110 Init
endmodule

module AccesRegistre (
  input  [3:0] _11,
  input  [3:0] _00,
  input  [3:0] _01,
  input  [3:0] _10,
  input  [1:0] Signal,
  output [3:0] Out
);

  Multiplexer #(.select(2), .width(4), .enable("false")) multiplexer_1 (
    .in0(_00), .in1(_01), .in2(_10), .in3(_11), .out(Out), .sel(Signal));
endmodule

// Decodeur
module DecodeurSansRam (
  input  [9:0] in_1,
  output [3:0] OP,
  output [1:0] B,
  output [1:0] A,
  output [1:0] Registre
);

  wire or_1_out, or_2_out, or_3_out;

  Demultiplexer #(.width(10), .enable("false")) demultiplexer_1 (
    .out1({Registre, A, B, OP}), .in(in_1), .sel(or_3_out));  // open: out0
  or or_1 (or_1_out, in_1[9], in_1[8], in_1[7], in_1[6], in_1[5]);
  or or_2 (or_2_out, in_1[4], in_1[3], in_1[2], in_1[1], or_1_out);
  or or_3 (or_3_out, or_2_out, in_1[0]);
endmodule

module Processeur (
  input  Start,
  input  [7:0] in_2,
  input  [14:0] in_3,
  input  in_4,
  input  in_5,
  output [7:0] out_6,
  output [7:0] out_7,
  output out_8,
  output out_9,
  output out_10
);

  wire Clock, Str, unitecommande_1_changeinstruction;
  wire [2:0] decodeur_1_signal;
  wire [3:0] ValueIn, ValueOut;
  wire [7:0] Adress;
  wire [11:0] decodeur_1_data;
  wire [14:0] ram_1_data;

  Clock clock_1 (.out(Clock));
  RAM #(.dataWidth(15)) ram_1 (.addr(out_6), .data(ram_1_data));  // open: sel, clk, ld, clr
  Traitement traitement_1 (.in_1(out_6), .Init(out_8), .\Terminé (out_10), .En_cours(out_9));
  Compteur8Bits compteur8bits_1 (
    .Instruction(out_7), .Clock(Clock), .ChargeInstruction(unitecommande_1_changeinstruction), .Start(Start),
    .Instructions(out_6));
  Decodeur decodeur_1 (.in_1(ram_1_data), .Signal(decodeur_1_signal), .Data(decodeur_1_data));
  UniteCommande unitecommande_1 (
    .Data(decodeur_1_data), .Signal(decodeur_1_signal), .Clock(Clock), .Instruction(out_7),
    .ChangeInstruction(unitecommande_1_changeinstruction), .Str(Str), .ValueRam(ValueOut), .Adress(Adress),
    .ValueToStock(ValueIn));
  RAM #(.dataWidth(4), .bus("separate")) ram_2 (
    .addr(Adress), .din(ValueIn), .data(ValueOut), .str(Str), .clk(Clock));  // open: sel, ld, clr
  RAM #(.dataWidth(15), .bus("separate")) ram_3 (
    .addr(in_2), .din(in_3), .str(in_4), .clk(in_5));  // open: data, sel, ld, clr

  // Other names for the same wires on the sheet: En_cours = out_9; Init = out_8; Terminé = out_10

  // Notes on the sheet:
  //   1000  OR
  //   0110 ADD
  //   0111 AND
  //   1001 XOR
  //   1010 Init
  //   0000 Multiplication
  //   0100 Soustraction
  //   0101 Retourne A
  //   1011 Egalité = : Z -> 1
  //   zzfzefzef
  //   Jeux d'instructions
  //   Déplacement de la case 01 dans la case 10
  //   Boucle si égale à 00 instruction (ADDITION DE 01 ET 10 DANS LE REGISTRE 11)
  //   110 Ret       12 b => Inutile
  //   000 Jump                  8 b => instruction to go
  //   001 Load ( M to R )    8 b => Adress / 2 b => registre / 2 b => Inutile
  //   010 Store ( R to M )   8 b => Adress / 2 b => regitre / 2 => Inutile
  //   2 b =>  choix / 10 b => Infos     ====> 12 b
  //   011  OP      2 b => Inutile / 2 b => Registre / 2 b => A / 2 b =>B / 4 b => OP 
  //   101 Move      2 b => registre a déplacer / 2 b => registre ou déplacer / 8 b => Inutile 
  //   100 Jump non si égalité    8 b => instruction to go / 2 b => registre comparaison / 2 b => registre comparaison
endmodule

module UniteCommande (
  input  [3:0] ValueRam,
  input  [11:0] Data,
  input  [2:0] Signal,
  input  Clock,
  output Str,
  output [7:0] Adress,
  output [3:0] ValueToStock,
  output [7:0] Instruction,
  output ChangeInstruction
);

  wire Clock_t, Z;
  wire [1:0] load_store_1_registre, RegisterA, RegisterB;
  wire [3:0] AccesRegistre_2_out, AccesRegistre_out, load_store_1_value, OP, Registre1, Registre2, Registre3,
       Registre4, ual_1_out;

  Load_Store load_store_1 (
    .ValeurAStocker(ual_1_out), .ValeurRam(ValueRam), .Data(Data), .Signal(Signal), .Clock(Clock),
    .Registre1(Registre1), .Registre2(Registre2), .Registre3(Registre3), .Registre4(Registre4), .in_10(Z),
    .Registre(load_store_1_registre), .Value(load_store_1_value), .Adress(Adress), .Str(Str),
    .Clock_2(Clock_t), .ChangeInstruction(ChangeInstruction), .OP(OP), .RegisterA(RegisterA),
    .RegsiterB(RegisterB), .ValueToStock(ValueToStock));
  AccesRegistre AccesRegistre (
    ._11(Registre4), ._00(Registre1), ._01(Registre2), ._10(Registre3), .Signal(RegisterA),
    .Out(AccesRegistre_out));
  Registre Registre (
    .Value(load_store_1_value), .Clock(Clock_t), .SignalRegistre(load_store_1_registre), .out_4(Registre1),
    .out_5(Registre2), .out_6(Registre3), .out_7(Registre4));
  AccesRegistre AccesRegistre_2 (
    ._11(Registre4), ._00(Registre1), ._01(Registre2), ._10(Registre3), .Signal(RegisterB),
    .Out(AccesRegistre_2_out));
  UAL ual_1 (.OP(OP), .A(AccesRegistre_out), .B(AccesRegistre_2_out), .Out(ual_1_out), .ZF(Z));  // open: Overflow, SF

  assign Instruction = Adress;

  // Notes on the sheet:
  //   100 OR
  //   010 ADD
  //   011 AND
  //   101 XOR
  //   110 Init
  //   000 Soustraction
  //   001 Retourne A
  //   111 Egalité = : Z -> 1
  //   110 Ret       12 b => Inutile
  //   000 Jump                  8 b => instruction to go
  //   001 Load ( M to R )    8 b => Adress / 2 b => registre / 2 b => Inutile
  //   010 Store ( R to M )   8 b => Adress / 2 b => regitre / 2 b Inutile
  //   3 b =>  choix / 12 b => Infos     ====> 15 b
  //   011  OP      3 b => Inutile / 2 b => Registre / 2 b => A / 2 b =>B / 3 b => OP 
  //   101 Move      2 b => registre a déplacer / 2 b => registre ou déplacer / 8 b => Inutile 
  //   100 Jump si égalité    8 b => instruction to go / 2 b => registre comparaison / 2 b => registre comparaison
endmodule

module Load_Store (
  input  [3:0] ValeurAStocker,
  input  [3:0] ValeurRam,
  input  [11:0] Data,
  input  [2:0] Signal,
  input  Clock,
  input  [3:0] Registre1,
  input  [3:0] Registre2,
  input  [3:0] Registre3,
  input  [3:0] Registre4,
  input  in_10,
  output [1:0] Registre,
  output [3:0] Value,
  output [7:0] Adress,
  output Str,
  output Clock_2,
  output ChangeInstruction,
  output [3:0] OP,
  output [1:0] RegisterA,
  output [1:0] RegsiterB,
  output [3:0] ValueToStock
);

  wire and_1_out, and_2_out, and_6_out, and_7_out, and_8_out, and_9_out, and_11_out, and_12_out,
       ChangeInstruction_t, Move, multiplexer_2_out, not_1_out, not_2_out, not_4_out, not_5_out, not_6_out,
       not_7_out, not_8_out, not_9_out, not_10_out, not_11_out, not_12_out, not_13_out, not_14_out,
       not_15_out, not_16_out, not_17_out, not_18_out, not_19_out, or_1_out, RegisterDirectionLocation,
       RegisterDirectionValue;
  wire [1:0] A, B, multiplexer_1_out, Registre_comparaison, Registre_t, RegistreADeplacer, RegistreL_S,
       RegistreOuDeplacer;
  wire [3:0] multiplexer_6_out, OP_t, registreMove;
  wire [7:4] demultiplexer_1_out0;
  wire [11:10] demultiplexer_1_out1;

  not not_1 (not_1_out, Signal[2]);
  and and_1 (and_1_out, Signal[0], Signal[1], not_1_out);
  Demultiplexer #(.width(12), .enable("false")) demultiplexer_1 (
    .out0({RegistreADeplacer, RegistreOuDeplacer, demultiplexer_1_out0, RegistreL_S, Registre_comparaison}),
    .out1({demultiplexer_1_out1, Registre_t, A, B, OP_t}), .in(Data), .sel(and_1_out));
  AccesRegistre AccesRegistre (
    ._11(Registre4), ._00(Registre1), ._01(Registre2), ._10(Registre3), .Signal(RegistreL_S),
    .Out(ValueToStock));
  AccesRegistre AccesRegistre_2 (
    ._11(Registre4), ._00(Registre1), ._01(Registre2), ._10(Registre3), .Signal(RegistreADeplacer),
    .Out(registreMove));
  Multiplexer #(.width(2), .enable("false")) multiplexer_1 (
    .in0(RegistreOuDeplacer), .in1(Registre_t), .out(multiplexer_1_out), .sel(Move));
  not not_2 (not_2_out, Signal[1]);
  Multiplexer #(.enable("false")) multiplexer_2 (
    .in0(ChangeInstruction_t), .in1(in_10), .out(multiplexer_2_out), .sel(and_6_out));
  not not_3 (Move, and_2_out);
  and and_2 (and_2_out, Signal[2], not_2_out, Signal[0]);
  not not_4 (not_4_out, Signal[1]);
  and and_3 (RegisterDirectionValue, Signal[0], not_5_out, not_6_out);
  not not_5 (not_5_out, Signal[1]);
  not not_6 (not_6_out, Signal[2]);
  not not_7 (not_7_out, Signal[2]);
  and and_4 (RegisterDirectionLocation, Signal[0], not_7_out, not_8_out);
  not not_8 (not_8_out, Signal[1]);
  not not_9 (not_9_out, Signal[0]);
  and and_5 (ChangeInstruction_t, not_9_out, not_10_out);
  not not_10 (not_10_out, Signal[1]);
  not not_11 (not_11_out, Signal[0]);
  not not_12 (not_12_out, Signal[1]);
  and and_6 (and_6_out, not_11_out, not_12_out, Signal[2]);
  Multiplexer #(.width(2), .enable("false")) multiplexer_3 (
    .in0(RegistreL_S), .in1(A), .out(RegisterA), .sel(Signal[0]));
  Multiplexer #(.width(2), .enable("false")) multiplexer_4 (
    .in0(Registre_comparaison), .in1(B), .out(RegsiterB), .sel(Signal[0]));
  Multiplexer #(.width(2), .enable("false")) multiplexer_5 (
    .in0(multiplexer_1_out), .in1(RegistreL_S), .out(Registre), .sel(RegisterDirectionLocation));
  Multiplexer #(.width(4), .enable("false")) multiplexer_6 (
    .in0(registreMove), .in1(ValeurAStocker), .out(multiplexer_6_out), .sel(Move));
  Multiplexer #(.width(4), .enable("false")) multiplexer_7 (
    .in0(multiplexer_6_out), .in1(ValeurRam), .out(Value), .sel(RegisterDirectionValue));
  not not_13 (not_13_out, Signal[2]);
  not not_14 (not_14_out, Signal[0]);
  not not_15 (not_15_out, Signal[2]);
  and and_7 (and_7_out, Signal[0], Signal[1], not_16_out);
  not not_16 (not_16_out, Signal[2]);
  not not_17 (not_17_out, Signal[1]);
  and and_8 (and_8_out, Signal[2], not_17_out, Signal[0]);
  Multiplexer #(.width(4), .enable("false")) multiplexer_8 (.in0(4'b1011), .in1(OP_t), .out(OP), .sel(Signal[0]));
  and and_9 (and_9_out, not_19_out, Signal[1], Signal[2]);
  and and_10 (Str, not_13_out, Signal[1], not_14_out);
  and and_11 (and_11_out, not_4_out, not_15_out, Signal[0]);
  not not_18 (not_18_out, Signal[0]);
  Multiplexer #(.width(8), .enable("false")) multiplexer_9 (
    .in0({RegistreADeplacer, RegistreOuDeplacer, demultiplexer_1_out0}), .in1({8{1'b1}}), .out(Adress),
    .sel(and_9_out));
  not not_19 (not_19_out, Signal[0]);
  Multiplexer #(.enable("false")) multiplexer_10 (
    .in0(multiplexer_2_out), .in1(and_12_out), .out(ChangeInstruction), .sel(and_12_out));
  and and_12 (and_12_out, not_18_out, Signal[1], Signal[2]);
  Demultiplexer #(.enable("false")) demultiplexer_2 (.out1(Clock_2), .in(Clock), .sel(or_1_out));  // open: out0
  or or_1 (or_1_out, and_11_out, and_8_out, and_7_out);

  // Other names for the same wires on the sheet: WhichEntry = Signal[0]; ValueRam[3:0] = ValeurRam; Z = in_10

  // Notes on the sheet:
  //   Envoi la donnée dans l'UAL ou dans le Load / Store
  //   100 OR
  //   010 ADD
  //   011 AND
  //   101 XOR
  //   110 Init
  //   111 Egalité = : Z -> 1
  //   110 Ret       12 b => Inutile
  //   2 b =>  choix / 10 b => Infos     ====> 12 b
  //   000 Jump                  8 b => instruction to go
  //   001 Load ( M to R )    8 b => Adress / 2 b => registre
  //   010 Store ( R to M )   8 b => Adress / 2 b => regitre
  //   100 Jump si égalité    8 b => instruction to go / 2 b => registre comparaison / 2 b => registre comparaison
  //   011  OP      2 b => Inutile / 2 b => Registre / 2 b => A / 2 b =>B / 4 b => OP 
  //   101 Move      2 b => registre a déplacer / 2 b => registre ou déplacer / 8 b => Inutile 
endmodule

module Decodeur (
  input  [14:0] in_1,
  output [2:0] Signal,
  output [11:0] Data
);

  wire or_1_out, or_2_out, or_3_out, or_4_out;

  Demultiplexer #(.width(15), .enable("false")) demultiplexer_1 (
    .out1({Signal, Data}), .in(in_1), .sel(or_4_out));  // open: out0
  or or_1 (or_1_out, in_1[14], in_1[13], in_1[12], in_1[11], in_1[10]);
  or or_2 (or_2_out, in_1[9], in_1[8], in_1[7], in_1[6], or_1_out);
  or or_3 (or_3_out, or_2_out, in_1[5], in_1[4], in_1[3], in_1[2]);
  or or_4 (or_4_out, or_3_out, in_1[1], in_1[0]);
endmodule

module Compteur8Bits (
  input  [7:0] Instruction,
  input  Clock,
  input  ChargeInstruction,
  input  Start,
  output [7:0] Instructions
);

  wire and_2_out, and_3_out, multiplexer_2_out, not_1_out, or_1_out, or_2_out;
  wire [7:0] Additionneur_out_3, and_1_out, multiplexer_1_out, multiplexer_3_out;

  or or_1 (or_1_out, ChargeInstruction, Start);
  or or_2 (or_2_out, Clock, and_3_out);
  Additionneur8Bits_1Bit Additionneur (.in_1(Clock), .in_2(Instructions), .out_3(Additionneur_out_3));
  Multiplexer #(.width(8), .enable("false")) multiplexer_1 (
    .in0(Additionneur_out_3), .in1(multiplexer_3_out), .out(multiplexer_1_out), .sel(or_1_out));
  not not_1 (not_1_out, or_2_out);
  Multiplexer #(.enable("false")) multiplexer_2 (.in0(not_1_out), .in1(Clock), .out(multiplexer_2_out), .sel(Start));
  Multiplexer #(.width(8), .enable("false")) multiplexer_3 (
    .in0({8{1'b0}}), .in1(Instruction), .out(multiplexer_3_out), .sel(ChargeInstruction));
  Registre8Bits registre8bits_1 (.In(multiplexer_1_out), .Clock(multiplexer_2_out), .Out(Instructions));
  assign and_1_out = {8{1'b1}} & Instructions;  // AND_Gate and_1, 8 bits wide
  and and_2 (and_2_out, and_1_out[7], and_1_out[6], and_1_out[5], and_1_out[4], and_1_out[3]);
  and and_3 (and_3_out, and_2_out, and_1_out[2], and_1_out[1], and_1_out[0]);
endmodule

module Traitement (
  input  [7:0] in_1,
  output Init,
  output \Terminé ,
  output En_cours
);

  wire and_1_out, and_2_out, or_1_out, or_2_out, or_3_out, or_4_out, or_5_out, or_6_out;

  or or_1 (or_1_out, in_1[7], in_1[6], in_1[5], in_1[4], in_1[3]);
  or or_2 (or_2_out, or_1_out, or_3_out);
  not not_1 (Init, or_2_out);
  or or_3 (or_3_out, in_1[2], in_1[1], in_1[0]);
  or or_4 (or_4_out, in_1[3], in_1[2], in_1[1], in_1[0]);
  or or_5 (or_5_out, in_1[7], in_1[6], in_1[5], in_1[4]);
  or or_6 (or_6_out, or_5_out, or_4_out);
  ExactlyOne xor_1 (.out(En_cours), .in0(or_6_out), .in3(\Terminé ), .in4(\Terminé ));
  and and_1 (and_1_out, in_1[7], in_1[6], in_1[5], in_1[4], in_1[3]);
  and and_2 (and_2_out, in_1[2], in_1[1], in_1[0]);
  and and_3 (\Terminé , and_1_out, and_2_out);
endmodule

module \TestEgalité  (
  input  [3:0] A,
  input  [3:0] B,
  output [4:0] out_3
);

  xor xor_1 (out_3[0], A[0], B[0]);
  xor xor_2 (out_3[1], A[1], B[1]);
  xor xor_3 (out_3[2], A[2], B[2]);
  xor xor_4 (out_3[3], A[3], B[3]);

  assign out_3[4] = 1'b0;

  // Other names for the same wires on the sheet: a1 = A[0]; a2 = A[1]; a3 = A[2]; a4 = A[3]; b1 = B[0]; b2 = B[1];
  //   b3 = B[2]; b4 = B[3]

  // Notes on the sheet:
  //   Permet de tester l'égalité entre deux nombres, renvoi 00000 quand c'est égale car il n'y a aucune différence et retourne les différence sinon.
  //   La constante ajouté corresponds à l'overflow
endmodule

// RetourneLavaleur
module RetourneVariable (
  input  [3:0] In,
  output [4:0] Out
);


  assign Out = {1'b0, In};
endmodule

module TestSupInfEquals (
  input  [3:0] A,
  input  [3:0] B,
  output A_B,
  output A_B_2,
  output A_B_3
);

  wire multiplexer_1_out, multiplexer_2_out, multiplexer_3_out, not_1_out, not_2_out, not_3_out, not_4_out,
       not_6_out, not_7_out, or_1_out, tablea_b_1_a_b, tablea_b_2_a_b, tablea_b_3_a_b, tablea_b_4_a_b,
       testsigneegalite_1_choixvaleur, testsigneegalite_2_choixvaleur, testsigneegalite_3_choixvaleur,
       testsigneegalite_4_choixvaleur;
  wire [4:0] \testegalité_1_out_3 ;

  TableA_B tablea_b_1 (.A(A[0]), .B(B[0]), .A_B(tablea_b_1_a_b));
  not not_1 (not_1_out, testsigneegalite_1_choixvaleur);
  TestSigneEgalite testsigneegalite_1 (.A(A[0]), .B(B[0]), .ChoixValeur(testsigneegalite_1_choixvaleur));
  Multiplexer #(.enable("false")) multiplexer_1 (
    .in0(tablea_b_1_a_b), .in1(1'b0), .out(multiplexer_1_out), .sel(not_1_out));
  TestSigneEgalite testsigneegalite_2 (.A(A[1]), .B(B[1]), .ChoixValeur(testsigneegalite_2_choixvaleur));
  TableA_B tablea_b_2 (.A(A[1]), .B(B[1]), .A_B(tablea_b_2_a_b));
  TestSigneEgalite testsigneegalite_3 (.A(A[2]), .B(B[2]), .ChoixValeur(testsigneegalite_3_choixvaleur));
  TableA_B tablea_b_3 (.A(A[2]), .B(B[2]), .A_B(tablea_b_3_a_b));
  not not_2 (not_2_out, testsigneegalite_2_choixvaleur);
  Multiplexer #(.enable("false")) multiplexer_2 (
    .in0(tablea_b_2_a_b), .in1(multiplexer_1_out), .out(multiplexer_2_out), .sel(not_2_out));
  TestSigneEgalite testsigneegalite_4 (.A(A[3]), .B(B[3]), .ChoixValeur(testsigneegalite_4_choixvaleur));
  TableA_B tablea_b_4 (.A(A[3]), .B(B[3]), .A_B(tablea_b_4_a_b));
  not not_3 (not_3_out, testsigneegalite_3_choixvaleur);
  Multiplexer #(.enable("false")) multiplexer_3 (
    .in0(tablea_b_3_a_b), .in1(multiplexer_2_out), .out(multiplexer_3_out), .sel(not_3_out));
  \TestEgalité  \testegalité_1  (.A(A), .B(B), .out_3(\testegalité_1_out_3 ));
  not not_4 (not_4_out, testsigneegalite_4_choixvaleur);
  Multiplexer #(.enable("false")) multiplexer_4 (
    .in0(tablea_b_4_a_b), .in1(multiplexer_3_out), .out(A_B), .sel(not_4_out));
  not not_5 (A_B_2, or_1_out);
  or or_1 (or_1_out, \testegalité_1_out_3 [0], \testegalité_1_out_3 [1], \testegalité_1_out_3 [2], \testegalité_1_out_3 [3], \testegalité_1_out_3 [4]);
  not not_6 (not_6_out, A_B_2);
  not not_7 (not_7_out, A_B);
  and and_1 (A_B_3, not_7_out, not_6_out);

  // Other names for the same wires on the sheet: a4 = A[0]; a3 = A[1]; a1 = A[3]; b4 = B[0]; b3 = B[1]; b1 = B[3]
endmodule

module TestSigneEgalite (
  input  A,
  input  B,
  output ChoixValeur
);

  wire and_1_out, and_2_out, not_1_out, not_2_out;

  not not_1 (not_1_out, B);
  not not_2 (not_2_out, A);
  and and_1 (and_1_out, A, not_1_out);
  and and_2 (and_2_out, not_2_out, B);
  or or_1 (ChoixValeur, and_1_out, and_2_out);
endmodule

module TableA_B (
  input  A,
  input  B,
  output A_B
);

  wire not_1_out;

  and and_1 (A_B, A, not_1_out);
  not not_1 (not_1_out, B);
endmodule

// Soustration
module Soustraction (
  input  [3:0] A,
  input  [3:0] B,
  output [4:0] Res,
  output \SF__Signed_Flag_1____Négatif 
);

  wire [2:0] testsupinfequals_1_a_b;
  wire [3:0] soustracteur4bits_1_res, soustracteur4bits_2_res;

  TestSupInfEquals testsupinfequals_1 (
    .A(A), .B(B), .A_B(testsupinfequals_1_a_b[0]), .A_B_2(testsupinfequals_1_a_b[1]),
    .A_B_3(testsupinfequals_1_a_b[2]));
  Soustracteur4bits soustracteur4bits_1 (.A(A), .B(B), .Res(soustracteur4bits_1_res));
  Soustracteur4bits soustracteur4bits_2 (.A(B), .B(A), .Res(soustracteur4bits_2_res));
  Multiplexer #(.select(3), .width(4), .enable("false")) multiplexer_1 (
    .in1(soustracteur4bits_1_res), .in2(4'b0000), .in4(soustracteur4bits_2_res), .out(Res[3:0]),
    .sel(testsupinfequals_1_a_b));  // open: in0, in3, in5, in6, in7
  Multiplexer #(.select(3), .enable("false")) multiplexer_2 (
    .in1(1'b0), .in2(1'b0), .in4(1'b1), .out(\SF__Signed_Flag_1____Négatif ), .sel(testsupinfequals_1_a_b));  // open: in0, in3, in5, in6, in7
  Hex_Digit_Display hex_digit_display_1 (.value(A));  // open: dp
  Hex_Digit_Display hex_digit_display_2 (.value(B));  // open: dp
  Hex_Digit_Display hex_digit_display_3 (.value(Res[3:0]));  // open: dp

  assign Res[4] = 1'b0;

  // Other names for the same wires on the sheet: Res_t[3:0] = Res[3:0]

  // Notes on the sheet:
  //   -----
  //   ======================
  //   A = 10
  //   B = 11
  //   C = 12
  //   D = 13
  //   E = 14
  //   F = 15
  //   Quand SF est à 1
  //   le chiffre est négatif
endmodule

module Soustracteur2Valeurs (
  input  A,
  input  B,
  output Res,
  output Retenue
);

  wire and_2_out, not_1_out, not_2_out;

  not not_1 (not_1_out, A);
  not not_2 (not_2_out, B);
  and and_1 (Retenue, not_1_out, B);
  and and_2 (and_2_out, A, not_2_out);
  or or_1 (Res, Retenue, and_2_out);
endmodule

module Soustracteur4bits (
  input  [3:0] A,
  input  [3:0] B,
  output [3:0] Res
);

  wire addictionneur2variables_1_res, addictionneur2variables_2_res, addictionneur2variables_3_res,
       and_1_out, and_2_out, multiplexer_1_out, multiplexer_2_out, multiplexer_3_out,
       soustracteur2valeurs_2_retenue, soustracteur2valeurs_3_retenue, soustracteur2valeurs_4_retenue;

  Hex_Digit_Display hex_digit_display_1 (.value(A));  // open: dp
  Hex_Digit_Display hex_digit_display_2 (.value(B));  // open: dp
  Addictionneur2Variables addictionneur2variables_1 (
    .in_1(1'b1), .in_2(B[3]), .Res(addictionneur2variables_1_res));  // open: Cout
  Multiplexer #(.enable("false")) multiplexer_1 (
    .in0(B[3]), .in1(addictionneur2variables_1_res), .out(multiplexer_1_out), .sel(and_1_out));
  and and_1 (and_1_out, Res[2], soustracteur2valeurs_2_retenue);
  Soustracteur2Valeurs soustracteur2valeurs_1 (.A(A[3]), .B(multiplexer_1_out), .Res(Res[3]));  // open: Retenue
  Addictionneur2Variables addictionneur2variables_2 (
    .in_1(1'b1), .in_2(B[2]), .Res(addictionneur2variables_2_res));  // open: Cout
  Multiplexer #(.enable("false")) multiplexer_2 (
    .in0(B[2]), .in1(addictionneur2variables_2_res), .out(multiplexer_2_out), .sel(and_2_out));
  and and_2 (and_2_out, Res[1], soustracteur2valeurs_3_retenue);
  Soustracteur2Valeurs soustracteur2valeurs_2 (
    .A(A[2]), .B(multiplexer_2_out), .Res(Res[2]), .Retenue(soustracteur2valeurs_2_retenue));
  Addictionneur2Variables addictionneur2variables_3 (
    .in_1(1'b1), .in_2(B[1]), .Res(addictionneur2variables_3_res));  // open: Cout
  Multiplexer #(.enable("false")) multiplexer_3 (
    .in0(B[1]), .in1(addictionneur2variables_3_res), .out(multiplexer_3_out),
    .sel(soustracteur2valeurs_4_retenue));
  Soustracteur2Valeurs soustracteur2valeurs_3 (
    .A(A[1]), .B(multiplexer_3_out), .Res(Res[1]), .Retenue(soustracteur2valeurs_3_retenue));
  Hex_Digit_Display hex_digit_display_3 (.value(Res));  // open: dp
  Soustracteur2Valeurs soustracteur2valeurs_4 (
    .A(A[0]), .B(B[0]), .Res(Res[0]), .Retenue(soustracteur2valeurs_4_retenue));

  // Other names for the same wires on the sheet: a1 = A[0]; a2 = A[1]; a3 = A[2]; a4 = A[3]; b1 = B[0]; b2 = B[1];
  //   b3 = B[2]; b4 = B[3]

  // Notes on the sheet:
  //   1000 - 0011 = 0101
endmodule

// Multiplicateur
module TestMultiplicateur (
  input  [3:0] A,
  input  [3:0] B,
  output [3:0] out_3
);

  wire [3:0] Res1, Res2, Res3, Res4;
  wire [4:0] additionneur4bits_1_out_3, additionneur4bits_2_out_3;
  wire [4:4] additionneur4bits_3_out_3;

  Multiplexer #(.width(4), .enable("false")) multiplexer_1 (.in0(4'b0000), .in1(A), .out(Res1), .sel(B[0]));
  Multiplexer #(.width(4), .enable("false")) multiplexer_2 (
    .in0(4'b0000), .in1({A[2:0], 1'b0}), .out(Res2), .sel(B[1]));
  Multiplexer #(.width(4), .enable("false")) multiplexer_3 (
    .in0(4'b0000), .in1({A[1:0], 2'b00}), .out(Res3), .sel(B[2]));
  Multiplexer #(.width(4), .enable("false")) multiplexer_4 (
    .in0(4'b0000), .in1({A[0], 3'b000}), .out(Res4), .sel(B[3]));
  Hex_Digit_Display hex_digit_display_1 (.value(A));  // open: dp
  Hex_Digit_Display hex_digit_display_2 (.value(B));  // open: dp
  Additionneur4bits additionneur4bits_1 (.in_1(Res1), .in_2(Res2), .out_3(additionneur4bits_1_out_3));
  Additionneur4bits additionneur4bits_2 (.in_1(Res3), .in_2(Res4), .out_3(additionneur4bits_2_out_3));
  Additionneur4bits additionneur4bits_3 (
    .in_1(additionneur4bits_1_out_3[3:0]), .in_2(additionneur4bits_2_out_3[3:0]),
    .out_3({additionneur4bits_3_out_3[4], out_3}));
  Hex_Digit_Display hex_digit_display_3 (.value(out_3));  // open: dp

  // Other names for the same wires on the sheet: b1 = B[0]; b2 = B[1]; b3 = B[2]; b4 = B[3]
endmodule
